# Fritzing sketch seed control schematics (saved by Fritzing 0.9.3b)
breadboards: 1

parts:
  Componente1 = Arduino BT
  Q1 = PNP-Transistor [package="TO92 [THT]"]
  Q2 = PNP-Transistor [package="TO92 [THT]"]
  Q3 = Basic FET P-Channel [package="TO220 [THT]"]
  D1 = Rectifier Diode [part_number=1N4001 package="300 mil [THT]"]
  R1 = Resistor [tolerance=±5% resistance=1k package=THT]
  R2 = Resistor [tolerance=±5% resistance=1k package=THT]
  R3 = Resistor [tolerance=±5% resistance=470 package=THT]
  R4 = Resistor [tolerance=±5% resistance=150 package=THT]
  R5 = Resistor [tolerance=±5% resistance=1k package=THT]
  J1 = Power Jack [package=power_jack_slot]
  M1 = DC Motor
  RHT1 = Humidity and Temperature Sensor RHT03

nets:
  N1: Componente1.D8, R5.Pin_1
  N2: Componente1.SS/PWM_D10, R2.Pin_0
  N3: Componente1.PWM_D6, Q2.C, R3.Pin_1
  N4: Componente1.RESET_WT11/D7, RHT1.Data-signal
  VIN: Componente1.VIN, R1.Pin_0, J1.GND, M1.pin_2
  N5: Componente1.GND, Q1.C, Q2.E, Q3.gate, J1.GNDBREAK, RHT1.GND_1
  3V3: Componente1.3V3, R3.Pin_0, RHT1.Vcc
  N6: Q1.E, R1.Pin_1
  N7: Q1.B, R2.Pin_1
  N8: Q2.B, R4.Pin_1
  N9: Q3.drain, D1.anode, M1.pin_1
  N10: Q3.source, D1.cathode, R5.Pin_0

notes:
  to water sensor
  Upper pin
  to water sensor
  Lower pin
